# Fritzing sketch MFRC522 connect wemos D1 esp32 (saved by Fritzing 0.9.3b)

parts:
  Componente1 = RFID-RC522-v2
  WeMos_D1_R1 = WeMos D1 R2

nets:
  N1: Componente1.SDA, WeMos_D1_R1.D14
  N2: Componente1.SCK, WeMos_D1_R1.D13
  N3: Componente1.MOSI, WeMos_D1_R1.D11
  N4: Componente1.MISO, WeMos_D1_R1.D12
  GND: Componente1.GND, WeMos_D1_R1.GND
  N5: Componente1.RST, WeMos_D1_R1.D9
  3.3V: Componente1.3.3V, WeMos_D1_R1.3.3V

custom parts:
  RFID-RC522-v2: A simple China made RFID-RC522 Reader; do check the pin labels, as this is a MFRC522 based clone.
  WeMos D1 R2: The D1 R2 is a mini wifi board based on the ESP-8266EX.
